// Logisim project branch-comp.circ as structural Verilog: 1 circuit, main circuit branch_comp
module branch_comp (
  input  [31:0] rs1,
  input  [31:0] rs2,
  input  BrUn,
  output BrEq,
  output BrLt
);

  wire Eq, Lt, UEq, ULt;

  Comparator #(.width(32)) comparator_1 (.a(rs1), .b(rs2), .eq(Eq), .lt(Lt));  // open: gt
  Comparator #(.mode("unsigned"), .width(32)) comparator_2 (.a(rs1), .b(rs2), .eq(UEq), .lt(ULt));  // open: gt
  Multiplexer #(.enable("false")) multiplexer_1 (.in0(Eq), .in1(UEq), .out(BrEq), .sel(BrUn));
  Multiplexer #(.enable("false")) multiplexer_2 (.in0(Lt), .in1(ULt), .out(BrLt), .sel(BrUn));

  // Notes on the sheet:
  //   INPUTS to your circuit
  //   Signed
  //   Unsigned
  //   DON'T CHANGE THE LOCATIONS OF THE INPUTS AND OUTPUTS!
  //   OUTPUT from your circuit
endmodule
