// Logisim project control-logic.circ as structural Verilog: 1 circuit, main circuit control_logic
module control_logic (
  input  [31:0] inst,
  input  BrEq,
  input  BrLt,
  output PCSel,
  output RegWEn,
  output [2:0] ImmSel,
  output BrUn,
  output ASel,
  output BSel,
  output [3:0] ALUSel,
  output MemRW,
  output [1:0] WBSel,
  output CSRSel,
  output CSRWen
);

  wire add_or_mul_or_sub_r, and_7_out, and_8_out, and_9_out, and_10_out, and_11_out, and_12_out, and_13_out,
       and_14_out, and_15_out, and_16_out, and_17_out, and_18_out, and_19_out, and_20_out, and_21_out,
       and_22_out, and_23_out, and_24_out, and_25_out, and_26_out, and_27_out, and_28_out, and_29_out,
       and_30_out, and_31_out, and_32_out, and_35_out, and_36_out, and_37_out, and_38_out, and_39_out,
       and_40_out, comparator_6_eq, comparator_15_eq, comparator_16_eq, comparator_17_eq, comparator_18_eq,
       comparator_19_eq, comparator_20_eq, comparator_21_eq, comparator_22_eq, comparator_23_eq,
       comparator_24_eq, comparator_25_eq, comparator_26_eq, comparator_27_eq, comparator_28_eq,
       comparator_29_eq, demultiplexer_5_out0, i_13_op_code, is_add, is_add_i, is_add_jalr, is_add_load,
       is_add_r, is_add_s, is_add_sb, is_add_u, is_add_uj, is_and, is_and_i, is_and_r, is_B, is_beq, is_bge,
       is_bgeu, is_blt, is_bltu, is_bne, is_i, is_mul, is_mul_r, is_mulh, is_mulh_r, is_mulhu, is_mulhu_r,
       is_or, is_or_i, is_or_r, is_or_r_i, is_r, is_sb, is_sll, is_sll_i, is_sll_r, is_slt, is_slt_i,
       is_slt_r, is_sra, is_sra_i, is_sra_r, is_srl, is_srl_i, is_srl_r, is_sub, is_sub_r, is_u, is_uj,
       is_xor, is_xor_i, is_xor_r, not_1_out, not_2_out, not_3_out, or_1_out, or_2_out, or_6_out, or_7_out,
       or_8_out, or_11_out, sll_or_mulh_r, srl_or_sra_i, srl_or_sra_r, zero_or_one_r, zero_or_two_i,
       zero_or_two_r;

  Comparator #(.width(7)) comparator_1 (.a(inst[6:0]), .b(7'b0110011), .eq(is_r));  // open: gt, lt
  Comparator #(.width(7)) comparator_2 (.a(inst[6:0]), .b(7'b0100011), .eq(MemRW));  // open: gt, lt
  Comparator #(.width(7)) comparator_3 (.a(inst[6:0]), .b(7'b1100011), .eq(is_sb));  // open: gt, lt
  Comparator #(.width(7)) comparator_4 (.a(inst[6:0]), .b(7'b1101111), .eq(is_uj));  // open: gt, lt
  Demultiplexer #(.enable("false"), .select(3)) demultiplexer_1 (
    .out0(add_or_mul_or_sub_r), .out1(sll_or_mulh_r), .out2(is_slt_r), .out3(is_mulhu_r), .out4(is_xor_r),
    .out5(srl_or_sra_r), .out6(is_or_r), .out7(is_and_r), .in(1'b1), .sel(inst[14:12]));
  BitSelector #(.width(7)) bitselector_1 (.in(inst[31:25]), .out(zero_or_two_r), .sel(3'b101));
  BitSelector #(.width(7)) bitselector_2 (.in(inst[31:25]), .out(zero_or_one_r), .sel(3'b000));
  Demultiplexer #(.enable("false"), .select(3)) demultiplexer_2 (
    .out0(is_add_i), .out1(is_sll_i), .out2(is_slt_i), .out4(is_xor_i), .out5(srl_or_sra_i), .out6(is_or_i),
    .out7(is_and_i), .in(1'b1), .sel(inst[14:12]));  // open: out3
  Comparator #(.width(7)) comparator_5 (.a(inst[6:0]), .b(7'b0010011), .eq(i_13_op_code));  // open: gt, lt
  Comparator #(.width(7)) comparator_6 (.a(inst[6:0]), .b(7'b1100011), .eq(comparator_6_eq));  // open: gt, lt
  Comparator #(.width(7)) comparator_7 (.a(inst[6:0]), .b(7'b0000011), .eq(is_add_load));  // open: gt, lt
  Comparator #(.width(7)) comparator_8 (.a(inst[6:0]), .b(7'b1100111), .eq(is_add_jalr));  // open: gt, lt
  Comparator #(.width(7)) comparator_9 (.a(inst[6:0]), .b(7'b0100011), .eq(is_add_s));  // open: gt, lt
  Comparator #(.width(7)) comparator_10 (.a(inst[6:0]), .b(7'b1100011), .eq(is_add_sb));  // open: gt, lt
  Comparator #(.width(7)) comparator_11 (.a(inst[6:0]), .b(7'b0010111), .eq(is_add_u));  // open: gt, lt
  Comparator #(.width(7)) comparator_12 (.a(inst[6:0]), .b(7'b0110111), .eq(is_B));  // open: gt, lt
  Comparator #(.width(7)) comparator_13 (.a(inst[6:0]), .b(7'b1101111), .eq(is_add_uj));  // open: gt, lt
  Comparator #(.width(7)) comparator_14 (.a(inst[6:0]), .b(7'b1110011), .eq(CSRWen));  // open: gt, lt
  Comparator #(.width(7)) comparator_15 (.a(inst[6:0]), .b(7'b0000011), .eq(comparator_15_eq));  // open: gt, lt
  Comparator #(.width(7)) comparator_16 (.a(inst[6:0]), .b(7'b0010011), .eq(comparator_16_eq));  // open: gt, lt
  Comparator #(.width(7)) comparator_17 (.a(inst[6:0]), .b(7'b1100111), .eq(comparator_17_eq));  // open: gt, lt
  Comparator #(.width(7)) comparator_18 (.a(inst[6:0]), .b(7'b1110011), .eq(comparator_18_eq));  // open: gt, lt
  Comparator #(.width(7)) comparator_19 (.a(inst[6:0]), .b(7'b0010111), .eq(comparator_19_eq));  // open: gt, lt
  Comparator #(.width(7)) comparator_20 (.a(inst[6:0]), .b(7'b0110111), .eq(comparator_20_eq));  // open: gt, lt
  BitSelector #(.width(12)) bitselector_3 (.in(inst[31:20]), .out(zero_or_two_i), .sel(4'b1010));
  Comparator #(.width(3)) comparator_21 (.a(inst[14:12]), .b(3'b110), .eq(comparator_21_eq));  // open: gt, lt
  Comparator #(.width(3)) comparator_22 (.a(inst[14:12]), .b(3'b111), .eq(comparator_22_eq));  // open: gt, lt
  Comparator #(.width(3)) comparator_23 (.a(inst[14:12]), .b(3'b000), .eq(comparator_23_eq));  // open: gt, lt
  Comparator #(.width(3)) comparator_24 (.a(inst[14:12]), .b(3'b001), .eq(comparator_24_eq));  // open: gt, lt
  Comparator #(.width(3)) comparator_25 (.a(inst[14:12]), .b(3'b100), .eq(comparator_25_eq));  // open: gt, lt
  Comparator #(.width(3)) comparator_26 (.a(inst[14:12]), .b(3'b101), .eq(comparator_26_eq));  // open: gt, lt
  Comparator #(.width(3)) comparator_27 (.a(inst[14:12]), .b(3'b110), .eq(comparator_27_eq));  // open: gt, lt
  Comparator #(.width(3)) comparator_28 (.a(inst[14:12]), .b(3'b111), .eq(comparator_28_eq));  // open: gt, lt
  or or_1 (or_1_out, comparator_15_eq, comparator_16_eq);
  or or_2 (or_2_out, comparator_17_eq, comparator_18_eq);
  or or_3 (is_u, comparator_19_eq, comparator_20_eq);
  and and_1 (is_beq, comparator_23_eq, is_add_sb);
  and and_2 (is_bne, comparator_24_eq, is_add_sb);
  and and_3 (is_blt, comparator_25_eq, is_add_sb);
  and and_4 (is_bge, comparator_26_eq, is_add_sb);
  and and_5 (is_bltu, comparator_27_eq, is_add_sb);
  and and_6 (is_bgeu, comparator_28_eq, is_add_sb);
  Demultiplexer #(.enable("false")) demultiplexer_3 (
    .out0(is_srl_r), .out1(is_sra_r), .in(srl_or_sra_r), .sel(zero_or_two_r));
  Demultiplexer #(.enable("false")) demultiplexer_4 (
    .out0(is_sll_r), .out1(is_mulh_r), .in(sll_or_mulh_r), .sel(zero_or_one_r));
  and and_7 (and_7_out, comparator_21_eq, comparator_6_eq);
  and and_8 (and_8_out, comparator_22_eq, comparator_6_eq);
  or or_4 (is_i, or_1_out, or_2_out);
  Demultiplexer #(.enable("false")) demultiplexer_5 (
    .out0(demultiplexer_5_out0), .out1(is_mul_r), .in(add_or_mul_or_sub_r), .sel(zero_or_one_r));
  Demultiplexer #(.enable("false")) demultiplexer_6 (
    .out0(is_srl_i), .out1(is_sra_i), .in(srl_or_sra_i), .sel(zero_or_two_i));
  or or_5 (BrUn, and_7_out, and_8_out);
  Demultiplexer #(.enable("false")) demultiplexer_7 (
    .out0(is_add_r), .out1(is_sub_r), .in(demultiplexer_5_out0), .sel(zero_or_two_r));
  Priority_Encoder priority_encoder_1 (
    .in0(is_i), .in1(MemRW), .in2(is_sb), .in3(is_u), .in4(is_uj), .in5(is_r), .out(ImmSel));  // open: in6, in7, en_in, gs, en_out
  or or_6 (or_6_out, is_add_r, is_add_i, is_add_s, is_add_sb, is_add_u, is_add_uj, is_slt_r, is_slt_i, is_xor_r, is_xor_i, is_or_r, is_or_r_i, is_and_r, is_and_i, is_mulhu_r, is_mulh_r, is_srl_r, is_srl_i, is_sra_r, is_sra_i, is_sll_r, is_sll_i, is_sub_r, is_mul_r);
  not not_1 (not_1_out, BrEq);
  not not_2 (not_2_out, BrLt);
  not not_3 (not_3_out, BrLt);
  and and_9 (and_9_out, is_beq, BrEq);
  and and_10 (and_10_out, is_bne, not_1_out);
  and and_11 (and_11_out, is_blt, BrLt);
  and and_12 (and_12_out, is_bltu, BrLt);
  and and_13 (and_13_out, is_bge, BrEq);
  and and_14 (and_14_out, is_bge, not_2_out);
  and and_15 (and_15_out, is_bgeu, BrEq);
  and and_16 (and_16_out, is_bgeu, not_3_out);
  and and_17 (and_17_out, is_add_r, is_r);
  and and_18 (and_18_out, is_add_load, is_i);
  and and_19 (and_19_out, is_add_jalr, is_i);
  and and_20 (and_20_out, is_add_i, i_13_op_code, is_i);
  and and_21 (and_21_out, is_add_s, MemRW);
  and and_22 (and_22_out, is_add_sb, is_sb);
  and and_23 (and_23_out, is_add_u, is_u);
  and and_24 (and_24_out, is_add_uj, is_uj);
  and and_25 (and_25_out, is_slt_r, is_r);
  and and_26 (and_26_out, is_slt_i, i_13_op_code, is_i);
  and and_27 (and_27_out, is_xor_r, is_r);
  and and_28 (and_28_out, is_xor_i, i_13_op_code, is_i);
  and and_29 (and_29_out, is_or_r, is_r);
  and and_30 (and_30_out, is_or_i, i_13_op_code, is_i);
  and and_31 (and_31_out, is_and_r, is_r);
  and and_32 (and_32_out, is_and_i, i_13_op_code, is_i);
  and and_33 (is_mulhu, is_mulhu_r, is_r);
  and and_34 (is_mulh, is_mulh_r, is_r);
  and and_35 (and_35_out, is_srl_r, is_r);
  and and_36 (and_36_out, is_srl_i, i_13_op_code, is_i);
  and and_37 (and_37_out, is_sra_r, is_r);
  and and_38 (and_38_out, is_sra_i, i_13_op_code, is_i);
  and and_39 (and_39_out, is_sll_r, is_r);
  and and_40 (and_40_out, is_sll_i, i_13_op_code, is_i);
  and and_41 (is_sub, is_sub_r, is_r);
  and and_42 (is_mul, is_mul_r, is_r);
  or or_7 (or_7_out, and_13_out, and_14_out);
  or or_8 (or_8_out, and_15_out, and_16_out);
  or or_9 (RegWEn, is_r, is_i, is_u, is_uj, is_B);
  or or_10 (ASel, is_sb, is_add_u, is_uj);
  or or_11 (or_11_out, is_uj, is_add_jalr);
  or or_12 (is_add, and_17_out, and_18_out, and_19_out, and_20_out, and_21_out, and_22_out, and_23_out, and_24_out);
  or or_13 (is_slt, and_25_out, and_26_out);
  or or_14 (is_xor, and_27_out, and_28_out);
  or or_15 (is_or, and_29_out, and_30_out);
  or or_16 (is_and, and_31_out, and_32_out);
  or or_17 (is_srl, and_35_out, and_36_out);
  or or_18 (is_sra, and_37_out, and_38_out);
  or or_19 (is_sll, and_39_out, and_40_out);
  or or_20 (PCSel, is_add_uj, is_add_jalr, and_9_out, and_10_out, and_11_out, and_12_out, or_7_out, or_8_out);
  or or_21 (BSel, is_i, MemRW, is_add_u, is_uj, is_sb, is_B);
  Priority_Encoder #(.select(2)) priority_encoder_2 (
    .in0(or_6_out), .in1(is_add_load), .in2(or_11_out), .out(WBSel));  // open: in3, gs, en_out, en_in
  Comparator #(.width(3)) comparator_29 (.a(inst[14:12]), .b(3'b101), .eq(comparator_29_eq));  // open: gt, lt
  and and_43 (CSRSel, CSRWen, comparator_29_eq);
  Priority_Encoder #(.select(4)) priority_encoder_3 (
    .in0(is_add), .in1(is_sll), .in2(is_slt), .in4(is_xor), .in5(is_srl), .in6(is_or), .in7(is_and),
    .in8(is_mul), .in9(is_mulh), .in11(is_mulhu), .in12(is_sub), .in13(is_sra), .in15(is_B), .out(ALUSel));  // open: in3, in10, in14, gs, en_out, en_in

  // Other names for the same wires on the sheet: is_csr = CSRWen; is_lui = is_B; is_s = MemRW

  // Notes on the sheet:
  //   INPUTS to your circuit
  //   Check if encoding is R
  //   Check if encoding is S
  //   Check if encoding is SB
  //   Check if encoding is UJ
  //   func3
  //   func7
  //   opcode
  //   func7 = 0100000 => BitSel => 1
  //   func7 = 0000001 => BitSel => 1
  //   opcode
  //   opcode
  //   func3
  //   opcode
  //   opcode
  //   opcode
  //   opcode
  //   opcode
  //   opcode
  //   opcode
  //   Set BrUn
  //   AULSel for S-type instuctions
  //   AULSel for SB-type instuctions
  //   AULSel for UJ-type instuctions
  //   Helper for CSR (I-type) instuctions
  //   DON'T CHANGE THE LOCATIONS OF THE INPUTS AND OUTPUTS!
  //   OUTPUT from your circuit
  //   imm
  //   AULSel for U-type instuctions
  //   AULSel for R-type instuctions
  //   AULSel for I-type instuctions (0x03 opecode)
  //   AULSel for I-type instuctions (0x067 opecode)
  //   AULSel for I-type instuctions (0x13 opecode)
  //   func3
  //   func3
  //   func3
  //   func3
  //   Change back to signed compare 
  //   Check if encoding is i
  //   Check if encoding is u
  //   func3
  //   func3
  //   func3
  //   func3
  //   imm = 000000100000 => BitSel => 1
  //   Set ImmSel
  //   0=I  1=S  2=SB  3=U  4=UJ 5=R
  //   Set PCSel
  //   Set RegWEn
  //   Set MemRW
  //   Set WBSel
  //   Set ASel
  //   Set BSel
  //   if jal or jalr wb pc+4
  //   if load wb memory value
  //   else wb arithmetic value
  //   0: Arithmetic  1: Memory Access  2: PC+4
  //   If func3 is 0x5, csrwi  else csrw
  //   Set CSRSel
  //   Set CSRWen
  //   CSRSel (0) = csrw  CSRSel(1) = csrwi
  //   Set ALUSel
endmodule
