// Logisim project cpu.circ as structural Verilog: 1 circuit, main circuit cpu
module cpu (
  input  clk,
  input  [31:0] INSTRUCTION,
  input  [31:0] READ_DATA,
  output [31:0] WRITE_ADDRESS,
  output [31:0] PROGRAM_COUNTER,
  output [31:0] ra,
  output [31:0] sp,
  output [31:0] t0,
  output [31:0] t1,
  output [31:0] t2,
  output [31:0] s0,
  output [31:0] s1,
  output [31:0] a0,
  output [31:0] tohost,
  output [3:0] WRITE_ENABLE,
  output [31:0] WRITE_DATA
);

  wire and_1_out, ASel, BrEq, BrLt, BrUn, BSel, comparator_1_eq, comparator_2_eq, comparator_2_lt, CSRSel,
       CSRWen, MemRW, PCSel, register_3_q, RegWEn, StoreSel;
  wire [1:0] bit_extender_2_out, bit_extender_3_out, WBSel;
  wire [2:0] bit_extender_5_out, ImmSel, store_size, subtractor_1_out;
  wire [3:0] ALUSel, byte_mask, halfword_mask, multiplexer_4_out;
  wire [4:0] bit_extender_4_out, multiplier_1_out;
  wire [31:0] adder_1_out, adder_2_out, bit_extender_1_out, bit_extender_6_out, bit_extender_7_out, imm,
       INSTRUCTION_CHECK, INSTRUCTION_EX, load_result, multiplexer_1_out, multiplexer_6_out,
       multiplexer_7_out, PROGRAM_COUNTER_EX, result, rs1_data, rs2_data, shifter_3_out;

  Adder #(.width(32)) adder_1 (.a(PROGRAM_COUNTER), .b(32'h4), .out(adder_1_out));  // open: cin, cout
  Multiplexer #(.enable("false"), .width(32)) multiplexer_1 (
    .in0(adder_1_out), .in1(WRITE_ADDRESS), .out(multiplexer_1_out), .sel(PCSel));
  Register #(.width(32)) PC (.D(multiplexer_1_out), .clk(clk), .Q(PROGRAM_COUNTER));  // open: en, clr
  Register #(.width(32)) register_1 (.D(PROGRAM_COUNTER), .clk(clk), .Q(PROGRAM_COUNTER_EX));  // open: en, clr
  Register #(.width(32)) register_2 (.D(INSTRUCTION), .clk(clk), .Q(INSTRUCTION_CHECK));  // open: en, clr
  Register #(.width(1)) register_3 (.D(PCSel), .clk(clk), .Q(register_3_q));  // open: en, clr
  Multiplexer #(.enable("false"), .width(32)) multiplexer_2 (
    .in0(INSTRUCTION_CHECK), .in1(32'h13), .out(INSTRUCTION_EX), .sel(register_3_q));
  control_logic control_logic_1 (
    .CSRWen(CSRWen), .PCSel(PCSel), .RegWEn(RegWEn), .ImmSel(ImmSel), .BrUn(BrUn), .ASel(ASel), .BSel(BSel),
    .ALUSel(ALUSel), .MemRW(MemRW), .WBSel(WBSel), .CSRSel(CSRSel), .inst(INSTRUCTION_EX), .BrEq(BrEq),
    .BrLt(BrLt));
  assign bit_extender_1_out = {{27{1'b0}}, INSTRUCTION_EX[19:15]};  // Bit_Extender bit_extender_1
  regfile regfile_1 (
    .rs1(INSTRUCTION_EX[19:15]), .rs2(INSTRUCTION_EX[24:20]), .rd(INSTRUCTION_EX[11:7]), .Write_Data(result),
    .RegWEn(RegWEn), .clk(clk), .ra(ra), .sp(sp), .t0(t0), .t1(t1), .t2(t2), .s0(s0), .s1(s1), .a0(a0),
    .Read_Data_1(rs1_data), .Read_Data_2(rs2_data));
  imm_gen imm_gen_1 (.inst(INSTRUCTION_EX), .ImmSel(ImmSel), .imm(imm));
  // csr csr_1: pin names not known; wires that end beside it: bit_extender_1_out, CSRWen, clk, tohost
  Bit_Extender #(.in_width(32), .out_width(2)) bit_extender_2 (.in(WRITE_ADDRESS), .out(bit_extender_2_out));
  Bit_Extender #(.in_width(32), .out_width(2)) bit_extender_3 (.in(WRITE_ADDRESS), .out(bit_extender_3_out));
  assign bit_extender_4_out = {{3{1'b0}}, WRITE_ADDRESS[1:0]};  // Bit_Extender bit_extender_4
  Shifter #(.width(4)) shifter_1 (.in(4'b0011), .\dist (bit_extender_2_out), .out(halfword_mask));
  Shifter #(.width(4)) shifter_2 (.in(4'b0001), .\dist (bit_extender_3_out), .out(byte_mask));
  Multiplier #(.width(5)) multiplier_1 (
    .a(bit_extender_4_out), .b(5'b01000), .out(multiplier_1_out));  // open: cin, cout
  Shifter #(.width(32)) shifter_3 (.in(rs2_data), .\dist (multiplier_1_out), .out(shifter_3_out));
  Comparator #(.mode("unsigned"), .width(2)) comparator_1 (
    .a(WRITE_ADDRESS[1:0]), .b(2'b00), .eq(comparator_1_eq));  // open: gt, lt
  Multiplexer #(.enable("false"), .width(32)) multiplexer_3 (
    .in0(shifter_3_out), .in1(rs2_data), .out(WRITE_DATA), .sel(comparator_1_eq));
  branch_comp branch_comp_1 (.rs1(rs1_data), .rs2(rs2_data), .BrUn(BrUn), .BrEq(BrEq), .BrLt(BrLt));
  Multiplexer #(.enable("false"), .select(2), .width(4)) multiplexer_4 (
    .in0(byte_mask), .in1(halfword_mask), .in2(4'b1111), .out(multiplexer_4_out), .sel(INSTRUCTION_EX[13:12]));  // open: in3
  Multiplexer #(.enable("false"), .select(2), .width(3)) multiplexer_5 (
    .in0(3'b001), .in1(3'b010), .in2(3'b100), .out(store_size), .sel(INSTRUCTION_EX[13:12]));  // open: in3
  assign bit_extender_5_out = {{1{1'b0}}, WRITE_ADDRESS[1:0]};  // Bit_Extender bit_extender_5
  Multiplexer #(.enable("false"), .width(32)) multiplexer_6 (
    .in0(rs1_data), .in1(PROGRAM_COUNTER_EX), .out(multiplexer_6_out), .sel(ASel));
  Multiplexer #(.enable("false"), .width(32)) multiplexer_7 (
    .in0(rs2_data), .in1(imm), .out(multiplexer_7_out), .sel(BSel));
  Subtractor #(.width(3)) subtractor_1 (.a(3'b100), .b(bit_extender_5_out), .out(subtractor_1_out));  // open: bin, bout
  Comparator #(.mode("unsigned"), .width(3)) comparator_2 (
    .a(store_size), .b(subtractor_1_out), .eq(comparator_2_eq), .lt(comparator_2_lt));  // open: gt
  alu alu_1 (.Result(WRITE_ADDRESS), .A(multiplexer_6_out), .B(multiplexer_7_out), .ALUSel(ALUSel));
  assign bit_extender_6_out = {{24{READ_DATA[7]}}, READ_DATA[7:0]};  // Bit_Extender bit_extender_6
  assign bit_extender_7_out = {{16{READ_DATA[15]}}, READ_DATA[15:0]};  // Bit_Extender bit_extender_7
  Multiplexer #(.enable("false"), .select(2), .width(32)) multiplexer_8 (
    .in0(bit_extender_6_out), .in1(bit_extender_7_out), .in2(READ_DATA), .out(load_result),
    .sel(INSTRUCTION_EX[13:12]));  // open: in3
  or or_1 (StoreSel, comparator_2_eq, comparator_2_lt);
  Multiplexer #(.enable("false"), .width(4)) multiplexer_9 (
    .in0(4'b0000), .in1(multiplexer_4_out), .out(WRITE_ENABLE), .sel(and_1_out));
  and and_1 (and_1_out, MemRW, StoreSel);
  Multiplexer #(.enable("false"), .select(2), .width(32)) multiplexer_10 (
    .in0(WRITE_ADDRESS), .in1(load_result), .in2(adder_2_out), .out(result), .sel(WBSel));  // open: in3
  Adder #(.width(32)) adder_2 (.a(PROGRAM_COUNTER_EX), .b(32'h4), .out(adder_2_out));  // open: cin, cout

  // Other names for the same wires on the sheet: rd[4:0] = INSTRUCTION_EX[11:7]; rs1[4:0] = INSTRUCTION_EX[19:15];
  //   rs2[4:0] = INSTRUCTION_EX[24:20]; offset[31:0] = WRITE_ADDRESS

  // Notes on the sheet:
  //   Output to IMEM
  //   IMEM (do **NOT** move this)
  //   Inputs from IMEM
  //   Inputs/Outputs for testing. Do **NOT** move these.
  //   ints: Instruction to be decoded
  //   RegWEn: Register Write Enable
  //   MemRW: Memory read or write
  //   BrUn: If branch is signed or unsigned
  //   BrLt: If branch evaluation was less than
  //   BrEq: If branch evaluation was equal to
  //   ImmSel: Tell ImmGen which type of encoding the immidate is
  //   BSel: Choose wether busB will be an immidiate or contents of register B
  //   ALUSel: Select which arithmetic instruction to preform
  //   ASel: Choose wether busB will be PC or contents of register A
  //   PCSel: Choose between regular incrementing or jumping
  //   WBSel: Choose which result (arithmetic or memory access) we want to write back into the register
  //   Outputs To DMEM
  //   DMEM (do **NOT** move this)
  //   Inputs From DMEM
  //   The default bit map
  //   The default bit map
  //   0: lb  1: lh  2: lw
  //   Tells us the location in the current word
  //   Output is the amount of space left in the word
  //   lb (0), lh(1), lw(2)
  //   If space left is greater than the store size not nop
  //   Set Write_EN mask
endmodule
