// Logisim project imm-gen.circ as structural Verilog: 1 circuit, main circuit imm_gen
module imm_gen (
  input  [31:0] inst,
  input  [2:0] ImmSel,
  output [31:0] imm
);

  wire [31:0] bit_extender_3_out, bit_extender_4_out, bit_extender_5_out, i_imm, s_imm, sb_imm, u_imm, uj_imm;

  assign i_imm = {{20{inst[31]}}, inst[31:20]};  // Bit_Extender bit_extender_1
  assign s_imm = {{20{inst[31]}}, {inst[31:25], inst[11:7]}};  // Bit_Extender bit_extender_2
  assign bit_extender_3_out = {{20{inst[31]}}, {inst[31], inst[7], inst[30:25], inst[11:8]}};  // Bit_Extender bit_extender_3
  assign bit_extender_4_out = {{12{1'b0}}, inst[31:12]};  // Bit_Extender bit_extender_4
  Shifter #(.width(32)) shifter_1 (.in(bit_extender_3_out), .\dist (5'b00001), .out(sb_imm));
  Shifter #(.width(32)) shifter_2 (.in(bit_extender_4_out), .\dist (5'b01100), .out(u_imm));
  assign bit_extender_5_out = {{12{inst[31]}}, {inst[31], inst[19:12], inst[20], inst[30:21]}};  // Bit_Extender bit_extender_5
  Shifter #(.width(32)) shifter_3 (.in(bit_extender_5_out), .\dist (5'b00001), .out(uj_imm));
  Multiplexer #(.enable("false"), .select(3), .width(32)) multiplexer_1 (
    .in0(i_imm), .in1(s_imm), .in2(sb_imm), .in3(u_imm), .in4(uj_imm), .out(imm), .sel(ImmSel));  // open: in5, in6, in7

  // Notes on the sheet:
  //   INPUTS to your circuit
  //   imm gen for i type
  //   imm gen for s type
  //   imm gen for sb type
  //   imm gen for u type
  //   imm gen for uj type
  //   DON'T CHANGE THE LOCATIONS OF THE INPUTS AND OUTPUTS!
  //   OUTPUT from your circuit
  //   0=I  1=S  2=SB  3=U  4=UJ 5=R
endmodule
