// Logisim project regfile.circ as structural Verilog: 1 circuit, main circuit regfile
module regfile (
  input  [4:0] rs1,
  input  [4:0] rs2,
  input  [4:0] rd,
  input  [31:0] Write_Data,
  input  RegWEn,
  input  clk,
  output [31:0] ra,
  output [31:0] sp,
  output [31:0] t0,
  output [31:0] t1,
  output [31:0] t2,
  output [31:0] s0,
  output [31:0] s1,
  output [31:0] a0,
  output [31:0] Read_Data_1,
  output [31:0] Read_Data_2
);

  wire w_en_x0, w_en_x1, w_en_x2, w_en_x3, w_en_x4, w_en_x5, w_en_x6, w_en_x7, w_en_x8, w_en_x9, w_en_x10,
       w_en_x11, w_en_x12, w_en_x13, w_en_x14, w_en_x15, w_en_x16, w_en_x17, w_en_x18, w_en_x19, w_en_x20,
       w_en_x21, w_en_x22, w_en_x23, w_en_x24, w_en_x25, w_en_x26, w_en_x27, w_en_x28, w_en_x29, w_en_x30,
       w_en_x31;
  wire [31:0] read_x0, read_x3, read_x4, read_x11, read_x12, read_x13, read_x14, read_x15, read_x16,
       read_x17, read_x18, read_x19, read_x20, read_x21, read_x22, read_x23, read_x24, read_x25, read_x26,
       read_x27, read_x28, read_x29, read_x30, read_x31, w_to_x0, w_to_x1, w_to_x2, w_to_x3, w_to_x4,
       w_to_x5, w_to_x6, w_to_x7, w_to_x8, w_to_x9, w_to_x10, w_to_x11, w_to_x12, w_to_x13, w_to_x14,
       w_to_x15, w_to_x16, w_to_x17, w_to_x18, w_to_x19, w_to_x20, w_to_x21, w_to_x22, w_to_x23, w_to_x24,
       w_to_x25, w_to_x26, w_to_x27, w_to_x28, w_to_x29, w_to_x30, w_to_x31;

  Demultiplexer #(.enable("false"), .select(5)) demultiplexer_1 (
    .out0(w_en_x0), .out1(w_en_x1), .out2(w_en_x2), .out3(w_en_x3), .out4(w_en_x4), .out5(w_en_x5),
    .out6(w_en_x6), .out7(w_en_x7), .out8(w_en_x8), .out9(w_en_x9), .out10(w_en_x10), .out11(w_en_x11),
    .out12(w_en_x12), .out13(w_en_x13), .out14(w_en_x14), .out15(w_en_x15), .out16(w_en_x16),
    .out17(w_en_x17), .out18(w_en_x18), .out19(w_en_x19), .out20(w_en_x20), .out21(w_en_x21),
    .out22(w_en_x22), .out23(w_en_x23), .out24(w_en_x24), .out25(w_en_x25), .out26(w_en_x26),
    .out27(w_en_x27), .out28(w_en_x28), .out29(w_en_x29), .out30(w_en_x30), .out31(w_en_x31), .in(RegWEn),
    .sel(rd));
  Multiplexer #(.enable("false"), .select(5), .width(32)) multiplexer_1 (
    .in0(read_x0), .in1(ra), .in2(sp), .in3(read_x3), .in4(read_x4), .in5(t0), .in6(t1), .in7(t2), .in8(s0),
    .in9(s1), .in10(a0), .in11(read_x11), .in12(read_x12), .in13(read_x13), .in14(read_x14), .in15(read_x15),
    .in16(read_x16), .in17(read_x17), .in18(read_x18), .in19(read_x19), .in20(read_x20), .in21(read_x21),
    .in22(read_x22), .in23(read_x23), .in24(read_x24), .in25(read_x25), .in26(read_x26), .in27(read_x27),
    .in28(read_x28), .in29(read_x29), .in30(read_x30), .in31(read_x31), .out(Read_Data_1), .sel(rs1));
  Demultiplexer #(.enable("false"), .select(5), .width(32)) demultiplexer_2 (
    .out0(w_to_x0), .out1(w_to_x1), .out2(w_to_x2), .out3(w_to_x3), .out4(w_to_x4), .out5(w_to_x5),
    .out6(w_to_x6), .out7(w_to_x7), .out8(w_to_x8), .out9(w_to_x9), .out10(w_to_x10), .out11(w_to_x11),
    .out12(w_to_x12), .out13(w_to_x13), .out14(w_to_x14), .out15(w_to_x15), .out16(w_to_x16),
    .out17(w_to_x17), .out18(w_to_x18), .out19(w_to_x19), .out20(w_to_x20), .out21(w_to_x21),
    .out22(w_to_x22), .out23(w_to_x23), .out24(w_to_x24), .out25(w_to_x25), .out26(w_to_x26),
    .out27(w_to_x27), .out28(w_to_x28), .out29(w_to_x29), .out30(w_to_x30), .out31(w_to_x31),
    .in(Write_Data), .sel(rd));
  Multiplexer #(.enable("false"), .select(5), .width(32)) multiplexer_2 (
    .in0(read_x0), .in1(ra), .in2(sp), .in3(read_x3), .in4(read_x4), .in5(t0), .in6(t1), .in7(t2), .in8(s0),
    .in9(s1), .in10(a0), .in11(read_x11), .in12(read_x12), .in13(read_x13), .in14(read_x14), .in15(read_x15),
    .in16(read_x16), .in17(read_x17), .in18(read_x18), .in19(read_x19), .in20(read_x20), .in21(read_x21),
    .in22(read_x22), .in23(read_x23), .in24(read_x24), .in25(read_x25), .in26(read_x26), .in27(read_x27),
    .in28(read_x28), .in29(read_x29), .in30(read_x30), .in31(read_x31), .out(Read_Data_2), .sel(rs2));
  Register #(.width(32)) x0 (.D(w_to_x0), .en(w_en_x0), .clk(clk), .Q(read_x0), .clr(1'b1));
  Register #(.width(32)) x4 (.D(w_to_x4), .en(w_en_x4), .clk(clk), .Q(read_x4));  // open: clr
  Register #(.width(32)) x8 (.D(w_to_x8), .en(w_en_x8), .clk(clk), .Q(s0));  // open: clr
  Register #(.width(32)) x12 (.D(w_to_x12), .en(w_en_x12), .clk(clk), .Q(read_x12));  // open: clr
  Register #(.width(32)) x16 (.D(w_to_x16), .en(w_en_x16), .clk(clk), .Q(read_x16));  // open: clr
  Register #(.width(32)) x20 (.D(w_to_x20), .en(w_en_x20), .clk(clk), .Q(read_x20));  // open: clr
  Register #(.width(32)) x24 (.D(w_to_x24), .en(w_en_x24), .clk(clk), .Q(read_x24));  // open: clr
  Register #(.width(32)) x28 (.D(w_to_x28), .en(w_en_x28), .clk(clk), .Q(read_x28));  // open: clr
  Register #(.width(32)) x1 (.D(w_to_x1), .en(w_en_x1), .clk(clk), .Q(ra));  // open: clr
  Register #(.width(32)) x5 (.D(w_to_x5), .en(w_en_x5), .clk(clk), .Q(t0));  // open: clr
  Register #(.width(32)) x9 (.D(w_to_x9), .en(w_en_x9), .clk(clk), .Q(s1));  // open: clr
  Register #(.width(32)) x13 (.D(w_to_x13), .en(w_en_x13), .clk(clk), .Q(read_x13));  // open: clr
  Register #(.width(32)) x17 (.D(w_to_x17), .en(w_en_x17), .clk(clk), .Q(read_x17));  // open: clr
  Register #(.width(32)) x21 (.D(w_to_x21), .en(w_en_x21), .clk(clk), .Q(read_x21));  // open: clr
  Register #(.width(32)) x25 (.D(w_to_x25), .en(w_en_x25), .clk(clk), .Q(read_x25));  // open: clr
  Register #(.width(32)) x29 (.D(w_to_x29), .en(w_en_x29), .clk(clk), .Q(read_x29));  // open: clr
  Register #(.width(32)) x2 (.D(w_to_x2), .en(w_en_x2), .clk(clk), .Q(sp));  // open: clr
  Register #(.width(32)) x6 (.D(w_to_x6), .en(w_en_x6), .clk(clk), .Q(t1));  // open: clr
  Register #(.width(32)) x10 (.D(w_to_x10), .en(w_en_x10), .clk(clk), .Q(a0));  // open: clr
  Register #(.width(32)) x14 (.D(w_to_x14), .en(w_en_x14), .clk(clk), .Q(read_x14));  // open: clr
  Register #(.width(32)) x18 (.D(w_to_x18), .en(w_en_x18), .clk(clk), .Q(read_x18));  // open: clr
  Register #(.width(32)) x22 (.D(w_to_x22), .en(w_en_x22), .clk(clk), .Q(read_x22));  // open: clr
  Register #(.width(32)) x26 (.D(w_to_x26), .en(w_en_x26), .clk(clk), .Q(read_x26));  // open: clr
  Register #(.width(32)) x30 (.D(w_to_x30), .en(w_en_x30), .clk(clk), .Q(read_x30));  // open: clr
  Register #(.width(32)) x3 (.D(w_to_x3), .en(w_en_x3), .clk(clk), .Q(read_x3));  // open: clr
  Register #(.width(32)) x7 (.D(w_to_x7), .en(w_en_x7), .clk(clk), .Q(t2));  // open: clr
  Register #(.width(32)) x11 (.D(w_to_x11), .en(w_en_x11), .clk(clk), .Q(read_x11));  // open: clr
  Register #(.width(32)) x15 (.D(w_to_x15), .en(w_en_x15), .clk(clk), .Q(read_x15));  // open: clr
  Register #(.width(32)) x19 (.D(w_to_x19), .en(w_en_x19), .clk(clk), .Q(read_x19));  // open: clr
  Register #(.width(32)) x23 (.D(w_to_x23), .en(w_en_x23), .clk(clk), .Q(read_x23));  // open: clr
  Register #(.width(32)) x27 (.D(w_to_x27), .en(w_en_x27), .clk(clk), .Q(read_x27));  // open: clr
  Register #(.width(32)) x31 (.D(w_to_x31), .en(w_en_x31), .clk(clk), .Q(read_x31));  // open: clr

  // Other names for the same wires on the sheet: read_data1[31:0] = Read_Data_1; read_data2[31:0] = Read_Data_2;
  //   read_reg1[4:0] = rs1; read_reg2[4:0] = rs2; read_x1[31:0] = ra; read_x2[31:0] = sp; read_x5[31:0] = t0;
  //   read_x6[31:0] = t1; read_x7[31:0] = t2; read_x8[31:0] = s0; read_x9[31:0] = s1; read_x10[31:0] = a0;
  //   write_en = RegWEn; write_reg[4:0] = rd

  // Notes on the sheet:
  //   INPUTS to your circuit
  //   Check if we write to reg
  //   DON'T CHANGE THE LOCATIONS OF THE INPUTS AND OUTPUTS!
  //   These are DEBUG/TEST outputs from your circuit.
  //   OUTPUTS from your circuit
  //   Read reg output and pass it on as read_data1
  //   Write to reg
  //   Read reg output and pass it on as read_data2
endmodule
