// Logisim project cpu-load_store_a_bunch.circ as structural Verilog: 1 circuit, main circuit run_main
module run_main (
  output [31:0] ra,
  output [31:0] sp,
  output [31:0] t0,
  output [31:0] t1,
  output [31:0] t2,
  output [31:0] s0,
  output [31:0] s1,
  output [31:0] a0,
  output [31:0] Requested_Address,
  output [31:0] Requested_Instruction,
  output [15:0] Time_Step,
  output halt
);

  wire clk;

  Clock clock_1 (.out(clk));
  // Probe on Requested_Address
  // cpu_harness cpu_harness_1: pin names not known; wires that end beside it: Requested_Instruction, clk, Requested_Address, ra, sp, t0, t1, t2, s0, s1, a0
  ROM #(.addrWidth(14), .dataWidth(32)) rom_1 (.addr(Requested_Address[15:2]), .data(Requested_Instruction));
  // Probe on Requested_Instruction
  Counter #(.max('hffff), .width(16)) counter_1 (.clk(clk), .Q(Time_Step));  // open: clr, load, up, count, D, carry
  Comparator #(.width(16)) comparator_1 (.a(Time_Step), .b(16'h53), .eq(halt));  // open: gt, lt

  // Other names for the same wires on the sheet: INSTRUCTION[31:0] = Requested_Instruction;
  //   PROGRAM_COUNTER[31:0] = Requested_Address

  // Notes on the sheet:
  //   contents of rom_1 (hex, n*v repeats v):
  //   7E528293 AAB337 AEE30313 AAB337 AEE30313 AAB3B7 AEE30393 AAB437 AEE30413 AAB4B7 AEE30493 AAB537
  //   AEE30513 AAB5B7 AEE30593 AAB637 AEE30613 AAB6B7 AEE30693 AAB737 AEE30713 AAB7B7 AEE30793 AAB837
  //   AEE30813 AAB8B7 AEE30893 AAB937 AEE30913 AAB9B7 AEE30993 AABA37 AEE30A13 AABAB7 AEE30A93 AABB37
  //   AEE30B13 AABBB7 AEE30B93 AABC37 AEE30C13 AABCB7 AEE30C93 AABD37 AEE30D13 AABDB7 AEE30D93 AABE37
  //   AEE30E13 AABEB7 AEE30E93 AABF37 AEE30F13 AABFB7 AEE30F93 628023 7280A3 828123 9281A3 A28223 B282A3
  //   C28323 D283A3 E28423 F284A3 1028523 11285A3 1228623 13286A3 1428723 15287A3 1628823 17288A3 1828923
  //   19289A3 1A28A23 1B28AA3 1C28B23 1D28BA3 1E28C23 1F28CA3
  //   Instruction Memory
  //   Halts Execution After Constant # of Clock Cycles
  //   Constant
endmodule
